# Fritzing sketch wifi (saved by Fritzing 0.9.3b)
breadboards: 1

parts:
  Part1 = Photon
  D1 = LED_BARGRAPH_10 [package=led_bargaph_10]
  R1 = Resistor [tolerance=±5% resistance=220 package="0402 [SMD]"]
  R2 = Resistor [tolerance=±5% resistance=220 package="2010 [SMD]"]
  R4 = Resistor [tolerance=±5% resistance=220 package="2512 [SMD]"]
  R5 = Resistor [tolerance=±5% resistance=220 package="2512 [SMD]"]
  R6 = Resistor [tolerance=±5% resistance=220 package="2512 [SMD]"]
  R7 = Resistor [tolerance=±5% resistance=220 package="2512 [SMD]"]
  R8 = Resistor [tolerance=±5% resistance=220 package="2512 [SMD]"]
  R11 = Resistor [tolerance=±5% resistance=220 package="2512 [SMD]"]
  R12 = Resistor [tolerance=±5% resistance=220 package="2512 [SMD]"]
  R13 = Resistor [tolerance=±5% resistance=220 package="2512 [SMD]"]

nets:
  N1: Part1.A0, D1.I_A
  N2: Part1.A1, D1.J_A
  N3: Part1.GND, R1.Pin_0, R2.Pin_0, R4.Pin_0, R5.Pin_0, R6.Pin_0, R7.Pin_0, R8.Pin_0, R11.Pin_0, R12.Pin_0, R13.Pin_0
  N4: Part1.D0, D1.A_A
  N5: Part1.D1, D1.B_A
  N6: Part1.D2, D1.C_A
  N7: Part1.D3, D1.D_A
  N8: Part1.D4, D1.E_A
  N9: Part1.D5, D1.F_A
  N10: Part1.D6, D1.G_A
  N11: Part1.D7, D1.H_A
  N12: D1.J_C, R1.Pin_1
  N13: D1.I_C, R4.Pin_1
  N14: D1.H_C, R2.Pin_1
  N15: D1.G_C, R8.Pin_1
  N16: D1.F_C, R7.Pin_1
  N17: D1.E_C, R6.Pin_1
  N18: D1.D_C, R5.Pin_1
  N19: D1.C_C, R11.Pin_1
  N20: D1.B_C, R12.Pin_1
  N21: D1.A_C, R13.Pin_1
